# Fritzing sketch ARDUINO_GENIUS (saved by Fritzing 0.9.6b)
breadboards: 1

parts:
  Part1 = Arduino Uno (Rev3)
  S1 = Pushbutton [package="[THT]"]
  S2 = Pushbutton [package="[THT]"]
  S3 = Pushbutton [package="[THT]"]
  S4 = Pushbutton [package="[THT]"]
  LED1 = LED - 5mm [color="Red (633nm)" current=0.030 package="5 mm [THT]"]
  LED2 = LED - 5mm [color="Green (570nm)" current=0.030 package="5 mm [THT]"]
  LED3 = LED - 5mm [color="Yellow (595nm)" current=0.030 package="5 mm [THT]"]
  LED4 = LED - 5mm [color="White (4500K)" current=0.030 package="5 mm [THT]"]
  R1 = Resistor [tolerance=±5% power=0.25 resistance=220 package=THT]
  J1 = Piezo Speaker
  R2 = Resistor [tolerance=±5% power=0.25 resistance=220 package=THT]
  R3 = Resistor [tolerance=±5% power=0.25 resistance=220 package=THT]
  R4 = Resistor [tolerance=±5% power=0.25 resistance=220 package=THT]

nets:
  N1: Part1.D8, S4.Pin_1, S4.Pin_2
  N2: Part1.D9_PWM, S3.Pin_1, S3.Pin_2
  N3: Part1.D10_PWM/SS, S1.Pin_1, S1.Pin_2
  N4: Part1.D11_PWM/MOSI, S2.Pin_1, S2.Pin_2
  N5: Part1.D13/SCK, J1.pin2
  N6: Part1.D2, LED2.anode
  N7: Part1.D3_PWM, LED3.anode
  N8: Part1.D4, LED1.anode
  N9: Part1.D5_PWM, LED4.anode
  N10: Part1.GND, S1.Pin_3, S1.Pin_4, S2.Pin_3, S2.Pin_4, S3.Pin_3, S3.Pin_4, S4.Pin_3, S4.Pin_4, R1.Pin_1, J1.pin1, R2.Pin_1, R3.Pin_1, R4.Pin_1
  N11: LED1.cathode, R2.Pin_0
  N12: LED2.cathode, R3.Pin_0
  N13: LED3.cathode, R1.Pin_0
  N14: LED4.cathode, R4.Pin_0
